// Logisim project not_gate_2bit.circ as structural Verilog: 1 circuit, main circuit main
module main (
  input  [1:0] in_1,
  output [1:0] out_2
);

  assign out_2 = ~in_1;  // NOT_Gate not_1, 2 bits wide
endmodule
