// Logisim project or_gate_2bit.circ as structural Verilog: 1 circuit, main circuit main
module main (
  input  [1:0] in_1,
  input  [1:0] in_2,
  output [1:0] out_3
);

  assign out_3 = in_1 | in_2;  // OR_Gate or_1, 2 bits wide
endmodule
