// Logisim project or_gate_4bit.circ as structural Verilog: 1 circuit, main circuit main
module main (
  input  [3:0] in_1,
  input  [3:0] in_2,
  output [3:0] out_3
);

  assign out_3 = in_1 | in_2;  // OR_Gate or_1, 4 bits wide
endmodule
